// Logisim project uP.circ as structural Verilog: 7 circuits, main circuit ALU
module main (
  input  [1:0] X,
  input  reset,
  input  [3:0] in_3,
  input  [7:0] in_4,
  input  [7:0] in_5,
  input  [1:0] Y,
  input  [15:0] Instruction
);

  wire clock_1_out;
  wire [7:0] alu_1_result, XRegister, YRegister;

  Clock clock_1 (.out(clock_1_out));
  // Probe on alu_1_result
  ALU alu_1 (
    .Y(in_5), .X(in_4), .Opcode(in_3), .reset(reset), .clock(clock_1_out), .Result(alu_1_result));  // open: flagRegister
  Register R0 (.D(alu_1_result));  // open: en, clk, Q, clr
  Register R2 (.D(alu_1_result));  // open: en, clk, Q, clr
  Register R1 (.D(alu_1_result));  // open: en, clk, Q, clr
  Register R3 (.D(alu_1_result));  // open: en, clk, Q, clr
  Multiplexer #(.select(2), .width(8)) multiplexer_1 (.out(XRegister), .sel(X));  // open: in0, in1, in2, in3
  Multiplexer #(.select(2), .width(8)) multiplexer_2 (.out(YRegister), .sel(Y));  // open: in0, in1, in2, in3

  // Other names for the same wires on the sheet: Opcode[3:0] = Instruction[15:12];
  //   regResult[1:0] = Instruction[11:10]
endmodule

module ALU (
  input  [7:0] Y,
  input  [7:0] X,
  input  [3:0] Opcode,
  input  reset,
  input  clock,
  output [7:0] Result,
  output [7:0] flagRegister
);

  wire and_1_out, and_2_out, not_1_out, OFlagN, OFlagP, xor_1_out, Zflag;
  wire [2:2] multiplexer_3_out;
  wire [7:0] adder8bits_1_result, and8bits_1_result, multiplexer_1_out, not8bits_1_result, or8bits_1_result,
       substractor8bits_1_result;

  Multiplexer #(.width(8)) multiplexer_1 (.in0(Y), .in1(8'h1), .out(multiplexer_1_out), .sel(and_1_out));
  and and_1 (and_1_out, Opcode[1], and_2_out);
  and and_2 (and_2_out, Opcode[2], not_1_out);
  not not_1 (not_1_out, Opcode[3]);
  Adder8bits adder8bits_1 (.Y(multiplexer_1_out), .X(X), .Result(adder8bits_1_result), .Overflow(OFlagP));  // open: Cin
  Substractor8bits substractor8bits_1 (
    .X(X), .Y(multiplexer_1_out), .Result(substractor8bits_1_result), .Underflow(OFlagN));  // open: Cin
  And8bits and8bits_1 (.X(X), .Y(multiplexer_1_out), .Result(and8bits_1_result));
  Or8bits or8bits_1 (.X(X), .Y(multiplexer_1_out), .Result(or8bits_1_result));
  Not8bits not8bits_1 (.X(X), .Result(not8bits_1_result));
  Multiplexer #(.select(4), .width(8)) multiplexer_2 (
    .in4(adder8bits_1_result), .in5(substractor8bits_1_result), .in6(adder8bits_1_result),
    .in7(substractor8bits_1_result), .in8(and8bits_1_result), .in9(or8bits_1_result),
    .in10(not8bits_1_result), .out(Result), .sel(Opcode));  // open: in0, in1, in2, in3, in11, in12, in13, in14, in15
  Multiplexer multiplexer_3 (.in0(OFlagP), .in1(OFlagN), .out(multiplexer_3_out[2]), .sel(Opcode[0]));
  xor xor_1 (xor_1_out, Opcode[2], Opcode[3]);
  Register register_1 (
    .D({{5{1'b0}}, multiplexer_3_out[2], Zflag, Result[7]}), .en(xor_1_out), .clk(clock), .Q(flagRegister),
    .clr(reset));
  nor nor_1 (Zflag, Result[7], Result[6], Result[5], Result[4], Result[3], Result[2], Result[1], Result[0]);

  // Other names for the same wires on the sheet: Nflag = Result[7]
endmodule

module Adder8bits (
  input  Cin,
  input  [7:0] Y,
  input  [7:0] X,
  output [7:0] Result,
  output Overflow
);

  wire adder_1_cout, adder_2_cout, adder_3_cout, adder_4_cout, adder_5_cout, adder_6_cout, adder_7_cout;

  Adder #(.width(1)) adder_1 (.a(Y[0]), .b(X[0]), .out(Result[0]), .cin(Cin), .cout(adder_1_cout));
  Adder #(.width(1)) adder_2 (.a(Y[1]), .b(X[1]), .out(Result[1]), .cin(adder_1_cout), .cout(adder_2_cout));
  Adder #(.width(1)) adder_3 (.a(Y[2]), .b(X[2]), .out(Result[2]), .cin(adder_2_cout), .cout(adder_3_cout));
  Adder #(.width(1)) adder_4 (.a(Y[3]), .b(X[3]), .out(Result[3]), .cin(adder_3_cout), .cout(adder_4_cout));
  Adder #(.width(1)) adder_5 (.a(Y[4]), .b(X[4]), .out(Result[4]), .cin(adder_4_cout), .cout(adder_5_cout));
  Adder #(.width(1)) adder_6 (.a(Y[5]), .b(X[5]), .out(Result[5]), .cin(adder_5_cout), .cout(adder_6_cout));
  Adder #(.width(1)) adder_7 (.a(Y[6]), .b(X[6]), .out(Result[6]), .cin(adder_6_cout), .cout(adder_7_cout));
  Adder #(.width(1)) adder_8 (.a(Y[7]), .b(X[7]), .out(Result[7]), .cin(adder_7_cout), .cout(Overflow));
endmodule

module Substractor8bits (
  input  Cin,
  input  [7:0] X,
  input  [7:0] Y,
  output [7:0] Result,
  output Underflow
);

  wire subtractor_1_bout, subtractor_2_bout, subtractor_3_bout, subtractor_4_bout, subtractor_5_bout,
       subtractor_6_bout, subtractor_7_bout;

  Subtractor #(.width(1)) subtractor_1 (.a(X[0]), .b(Y[0]), .out(Result[0]), .bin(Cin), .bout(subtractor_1_bout));
  Subtractor #(.width(1)) subtractor_2 (
    .a(X[1]), .b(Y[1]), .out(Result[1]), .bin(subtractor_1_bout), .bout(subtractor_2_bout));
  Subtractor #(.width(1)) subtractor_3 (
    .a(X[2]), .b(Y[2]), .out(Result[2]), .bin(subtractor_2_bout), .bout(subtractor_3_bout));
  Subtractor #(.width(1)) subtractor_4 (
    .a(X[3]), .b(Y[3]), .out(Result[3]), .bin(subtractor_3_bout), .bout(subtractor_4_bout));
  Subtractor #(.width(1)) subtractor_5 (
    .a(X[4]), .b(Y[4]), .out(Result[4]), .bin(subtractor_4_bout), .bout(subtractor_5_bout));
  Subtractor #(.width(1)) subtractor_6 (
    .a(X[5]), .b(Y[5]), .out(Result[5]), .bin(subtractor_5_bout), .bout(subtractor_6_bout));
  Subtractor #(.width(1)) subtractor_7 (
    .a(X[6]), .b(Y[6]), .out(Result[6]), .bin(subtractor_6_bout), .bout(subtractor_7_bout));
  Subtractor #(.width(1)) subtractor_8 (.a(X[7]), .b(Y[7]), .out(Result[7]), .bin(subtractor_7_bout), .bout(Underflow));
endmodule

module And8bits (
  input  [7:0] X,
  input  [7:0] Y,
  output [7:0] Result
);

  assign Result = X & Y;  // AND_Gate and_1, 8 bits wide
endmodule

module Or8bits (
  input  [7:0] X,
  input  [7:0] Y,
  output [7:0] Result
);

  assign Result = X | Y;  // OR_Gate or_1, 8 bits wide
endmodule

module Not8bits (
  input  [7:0] X,
  output [7:0] Result
);

  assign Result = ~X;  // NOT_Gate not_1, 8 bits wide
endmodule
